// Digital circuit 2-Bit Mulitplier.dig as structural Verilog
module _2_Bit_Mulitplier (
  input  A0,
  input  B0,
  input  A1,
  input  B1,
  input  A0_2,
  input  B0_2,
  input  A1_2,
  input  B1_2,
  input  A0_3,
  input  B0_3,
  input  A1_3,
  input  B1_3,
  input  A0_4,
  input  B0_4,
  input  A1_4,
  input  B1_4,
  output P2,
  output P1,
  output P3,
  output P0
);

  wire and_2_out, and_3_out, and_5_out, and_6_out, and_7_out, and_8_out, not_1_out, not_2_out, not_3_out,
       not_4_out, not_5_out, not_6_out;

  and and_1 (P0, A0_4, B0_4);
  not not_1 (not_1_out, A0_2);
  not not_2 (not_2_out, A1_2);
  not not_3 (not_3_out, B0_2);
  not not_4 (not_4_out, B1_2);
  not not_5 (not_5_out, A0);
  not not_6 (not_6_out, B0);
  and and_2 (and_2_out, A1, not_5_out, B1);
  and and_3 (and_3_out, B1, not_6_out, A1);
  and and_4 (P3, A0_3, A1_3, B0_3, B1_3);
  and and_5 (and_5_out, B1_2, not_3_out);
  and and_6 (and_6_out, not_1_out, B0_2);
  and and_7 (and_7_out, A1_2, B0_2);
  and and_8 (and_8_out, not_1_out, B1_2);
  or or_1 (P2, and_2_out, and_3_out);
  or or_2 (P1, and_5_out, and_6_out, and_7_out, and_8_out);
endmodule
